# Fritzing sketch BinocularsHUD (saved by Fritzing 0.9.2b)
breadboards: 1

parts:
  PCB2 = RTC_DS1302_module
  Part1 = Arduino Due (Rev2b)
  Part2 = OLED Monochrome 128x64 0.96 inch [part_number=326]  # not connected

nets:
  N1: PCB2.VCC, Part1.IOREF
  GND: PCB2.GND, Part1.GND
  N2: PCB2.RST, Part1.D5_PWM
  N3: PCB2.DAT, Part1.D6_PWM
  N4: PCB2.CLK, Part1.D7_PWM

custom parts:
  RTC_DS1302_module: Arduino module DS1302 SPI Real Time Clock
  OLED Monochrome 128x64 0.96 inch: These displays are small, only about 1" diameter, but very readable due to the high contrast of an OLED display. This display is made of 128x64 individual white OLED pixels, each one is turned on or off by the controller chip. Because the display makes its own light, no backlight is required. This reduces the power required to run the OLED and is why the display has such high contrast; we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
